# Fritzing sketch CapSense Piano (saved by Fritzing 0.9.3b)
breadboards: 1

parts:
  Part1 = Arduino Uno (Rev3) - ICSP
  LED1 = LED - 5mm [color="Red (633nm)" package="5 mm [THT]"]
  R1 = Resistor [tolerance=±5% resistance=330 package=THT]
  SP1 = SPEAKER [package=pcb_mount_speaker]
  R2 = Trimmer Potentiometer [maximum_resistance=1kΩ package=THT]
  R3 = Resistor [tolerance=±5% resistance=1M package=THT]
  R4 = Resistor [tolerance=±5% resistance=1M package=THT]
  R5 = Resistor [tolerance=±5% resistance=1M package=THT]
  R6 = Resistor [tolerance=±5% resistance=1M package=THT]
  R7 = Resistor [tolerance=±5% resistance=1M package=THT]
  R8 = Resistor [tolerance=±5% resistance=1M package=THT]
  R9 = Resistor [tolerance=±5% resistance=1M package=THT]
  R10 = Resistor [tolerance=±5% resistance=1M package=THT]
  R12 = Resistor [tolerance=±5% resistance=1M package=THT]

nets:
  N1: Part1.A0, LED1.anode
  C: Part1.D8, R7.Pin_1
  D: Part1.D9_PWM, R10.Pin_1
  E: Part1.D10_PWM/SS, R9.Pin_1
  N2: Part1.D11_PWM/MOSI, R2.leg2
  Octave +: Part1.D12/MISO, R12.Pin_1
  N3: Part1.GND, R1.Pin_1, SP1.+
  N4: Part1.D2, R3.Pin_0, R4.Pin_0, R5.Pin_0, R6.Pin_0, R7.Pin_0, R8.Pin_0, R9.Pin_0, R10.Pin_0, R12.Pin_0
  Octave -: Part1.D3_PWM, R3.Pin_1
  F: Part1.D4, R4.Pin_1
  G: Part1.D5_PWM, R5.Pin_1
  A: Part1.D6_PWM, R6.Pin_1
  B: Part1.D7, R8.Pin_1
  N5: LED1.cathode, R1.Pin_0
  N6: SP1.-, R2.wiper
